# Fritzing sketch Protoipo 1 Componentes y PCB (saved by Fritzing 0.9.3b)
circuit board: 8.5cm x 8.5cm
breadboards: 2

parts:
  Arduino_Pro_Mini = Arduino Pro Mini v13
  Micro_SD_Header = female pin header, 6 pins [form="♀ (female)"]
  MosFetMotor = Basic FET P-Channel [package="TO220 [THT]"]
  Power_12V = Camdenboss CTB0158-2 [part_number=CTB0158-2 package=THT]
  Motor = Camdenboss CTB0158-2 [part_number=CTB0158-2 package=THT]
  R1-PullDown = Resistor [tolerance=±5% resistance=10k package=THT]
  SigM = Resistor [tolerance=±5% resistance=1k package=THT]
  GPS_7M_Header = female pin header, 5 pins [form="♀ (female)"]
  ADC4 = female pin header, 2 pins [form="♀ (female)"]
  ADC3 = female pin header, 2 pins [form="♀ (female)"]
  ADC2 = female pin header, 2 pins [form="♀ (female)"]
  ADC1 = female pin header, 2 pins [form="♀ (female)"]
  adcR4 = Resistor [tolerance=±1% resistance=150 package=THT]
  adcR3 = Resistor [tolerance=±1% resistance=150 package=THT]
  adcR2 = Resistor [tolerance=±1% resistance=150 package=THT]
  adcR1 = Resistor [tolerance=±1% resistance=150 package=THT]
  I2C-2 = female pin header, 4 pins [form="♀ (female)"]
  I2C-1 = female pin header, 4 pins [form="♀ (female)"]
  BuckConverter = female pin header, 4 pins [form="♀ (female)"]
  LoadSensor = Camdenboss CTB0158-2 [part_number=CTB0158-2 package=THT]
  R2-PullDown = Resistor [tolerance=±5% resistance=10k package=THT]
  SigS = Resistor [tolerance=±5% resistance=1k package=THT]
  MosfetSensor = Basic FET P-Channel [package="TO220 [THT]"]

nets:
  N1: Arduino_Pro_Mini.A4, I2C-2.pin3, I2C-1.pin3
  N2: Arduino_Pro_Mini.A5, I2C-2.pin2, I2C-1.pin2
  N3: Arduino_Pro_Mini.GND, Micro_SD_Header.pin6, MosFetMotor.source, Power_12V.pin1, R1-PullDown.Pin_0, GPS_7M_Header.pin4, ADC4.pin1, ADC3.pin1, ADC2.pin1, ADC1.pin1, adcR4.Pin_1, adcR3.Pin_1, adcR2.Pin_1, adcR1.Pin_1, I2C-2.pin4, I2C-1.pin4, BuckConverter.pin3, R2-PullDown.Pin_1, MosfetSensor.source
  N4: Arduino_Pro_Mini.VCC, Micro_SD_Header.pin1, GPS_7M_Header.pin5, I2C-2.pin1, I2C-1.pin1, BuckConverter.pin4
  N5: Arduino_Pro_Mini.A3, ADC4.pin2, adcR4.Pin_0
  N6: Arduino_Pro_Mini.A2, ADC3.pin2, adcR3.Pin_0
  N7: Arduino_Pro_Mini.A1, ADC2.pin2, adcR2.Pin_0
  N8: Arduino_Pro_Mini.A0, ADC1.pin2, adcR1.Pin_0
  N9: Arduino_Pro_Mini.D13/SCK, Micro_SD_Header.pin4
  N10: Arduino_Pro_Mini.D12/MISO, Micro_SD_Header.pin5
  N11: Arduino_Pro_Mini.D11_PWM/MOSI, Micro_SD_Header.pin3
  N12: Arduino_Pro_Mini.D10_PWM/SS, Micro_SD_Header.pin2
  N13: Arduino_Pro_Mini.D8, GPS_7M_Header.pin3
  N14: Arduino_Pro_Mini.D6_PWM, SigS.Pin_0
  N15: Arduino_Pro_Mini.D3_PWM, SigM.Pin_0
  N16: MosFetMotor.gate, R1-PullDown.Pin_1, SigM.Pin_1
  N17: MosFetMotor.drain, Motor.pin1
  N18: Power_12V.pin2, Motor.pin2, BuckConverter.pin2, LoadSensor.pin2
  N19: LoadSensor.pin1, MosfetSensor.drain
  N20: R2-PullDown.Pin_0, SigS.Pin_1, MosfetSensor.gate

notes:
  Sensor Logger
  Maker: Juan Pleitez
  +
